// Logisim project det_sequencia.circ as structural Verilog: 1 circuit, main circuit detector_sequencia_101
module detector_sequencia_101 (
  input  ENTRADA,
  output \saída 
);

  wire and_1_out, clock_1_out, d0_q, d1_q, not_1_out;

  Clock clock_1 (.out(clock_1_out));
  D_Flip_Flop d0 (.clk(clock_1_out), .D(ENTRADA), .Q(d0_q));  // open: Qn, preset, en, reset
  not not_1 (not_1_out, ENTRADA);
  D_Flip_Flop d1 (.clk(clock_1_out), .D(and_1_out), .Q(d1_q));  // open: Qn, preset, en, reset
  and and_1 (and_1_out, d0_q, not_1_out);
  and and_2 (\saída , d1_q, ENTRADA);
endmodule
