// Logisim project detector_numero_primo.circ as structural Verilog: 1 circuit, main circuit detector_num_primo
module detector_num_primo (
  input  ENTRADA,
  input  in_2,
  input  in_3,
  input  in_4,
  output \SAÍDA 
);

  wire and_1_out, and_2_out, and_3_out, and_4_out;

  and and_1 (and_1_out, ~ENTRADA, ~in_2, in_3);  // AND_Gate
  and and_2 (and_2_out, in_2, ~in_3, in_4);  // AND_Gate
  and and_3 (and_3_out, ~in_2, in_3, in_4);  // AND_Gate
  and and_4 (and_4_out, ~ENTRADA, in_2, in_4);  // AND_Gate
  or or_1 (\SAÍDA , and_1_out, and_2_out, and_3_out, and_4_out);
endmodule
