// Logisim project somador_8_bits.circ as structural Verilog: 2 circuits, main circuit somador_8_bits
module somador_8_bits (
  input  [7:0] A,
  input  [7:0] B,
  output [7:0] S,
  output overflow
);

  wire full_adder_1_carry_out, full_adder_2_carry_out, full_adder_3_carry_out, full_adder_4_carry_out,
       full_adder_5_carry_out, full_adder_6_carry_out, full_adder_7_carry_out;

  full_adder full_adder_1 (.S(S[0]), .CARRY_OUT(full_adder_1_carry_out), .A(A[0]), .B(B[0]), .CARRY_IN(1'b0));
  full_adder full_adder_2 (
    .S(S[1]), .CARRY_OUT(full_adder_2_carry_out), .A(A[1]), .B(B[1]), .CARRY_IN(full_adder_1_carry_out));
  full_adder full_adder_3 (
    .S(S[2]), .CARRY_OUT(full_adder_3_carry_out), .A(A[2]), .B(B[2]), .CARRY_IN(full_adder_2_carry_out));
  full_adder full_adder_4 (
    .S(S[3]), .CARRY_OUT(full_adder_4_carry_out), .A(A[3]), .B(B[3]), .CARRY_IN(full_adder_3_carry_out));
  full_adder full_adder_5 (
    .S(S[4]), .CARRY_OUT(full_adder_5_carry_out), .A(A[4]), .B(B[4]), .CARRY_IN(full_adder_4_carry_out));
  full_adder full_adder_6 (
    .S(S[5]), .CARRY_OUT(full_adder_6_carry_out), .A(A[5]), .B(B[5]), .CARRY_IN(full_adder_5_carry_out));
  full_adder full_adder_7 (
    .S(S[6]), .CARRY_OUT(full_adder_7_carry_out), .A(A[6]), .B(B[6]), .CARRY_IN(full_adder_6_carry_out));
  full_adder full_adder_8 (.S(S[7]), .CARRY_OUT(overflow), .A(A[7]), .B(B[7]), .CARRY_IN(full_adder_7_carry_out));
endmodule

module full_adder (
  input  A,
  input  B,
  input  CARRY_IN,
  output S,
  output CARRY_OUT
);

  wire and_1_out, and_2_out, xor_1_out;

  xor xor_1 (xor_1_out, A, B);
  and and_1 (and_1_out, CARRY_IN, xor_1_out);
  and and_2 (and_2_out, B, A);
  xor xor_2 (S, xor_1_out, CARRY_IN);
  or or_1 (CARRY_OUT, and_1_out, and_2_out);
endmodule
